# Fritzing sketch LCD (saved by Fritzing 0.9.3b)
breadboards: 1

parts:
  Part1 = Adafruit Metro M0 Express
  LCD_Backpack1 = LCD Backpack [part_number="LCM1602 IIC" chip_label="LCM1602 IIC" package="DIP (Dual Inline) [THT]"]
  S1 = Pushbutton [package="[SMD]"]
  S2 = Pushbutton [package="[SMD]"]

nets:
  N1: Part1.A0, LCD_Backpack1.SDA
  N2: Part1.A2, LCD_Backpack1.SCL
  GND: Part1.GND, LCD_Backpack1.GND, S1.Pin_1, S1.Pin_2, S2.Pin_1, S2.Pin_2
  N3: Part1.D2, S1.Pin_3, S1.Pin_4
  N4: Part1.D1, S2.Pin_3, S2.Pin_4
  +5V: Part1.+5V, LCD_Backpack1.VCC

custom parts:
  Adafruit Metro M0 Express: Metro is our series of microcontroller boards for use with the Arduino IDE. This new Metro board looks a whole lot like our original Metro 328, but with a huge upgrade. Instead of the ATmega328, this Metro features a ATSAMD21G18 chip, an ARM Cortex M0+. It's our first Metro that is designed for use with CircuitPython! CircuitPython is our beginner-oriented flavor of MicroPython - and as the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
  LCD Backpack: I2C-Module to use a 1602 or 2004 LCD on with the wire.h library Serial LCD Modul
