# Fritzing sketch rgbled (saved by Fritzing 0.9.3b)
breadboards: 1

parts:
  Part1 = Adafruit Metro M0 Express
  R1 = Resistor [tolerance=±5% resistance=220 package=THT]
  R2 = Resistor [tolerance=±5% resistance=220 package=THT]
  R3 = Resistor [tolerance=±5% resistance=220 package=THT]
  LED1 = RGB LED (com. anode, rbg) [package="5 mm [THT]"]
  R4 = Resistor [tolerance=±5% resistance=220 package=THT]
  R5 = Resistor [tolerance=±5% resistance=220 package=THT]
  R6 = Resistor [tolerance=±5% resistance=220 package=THT]
  LED2 = RGB LED (com. anode, rbg) [package="5 mm [THT]"]

nets:
  N1: Part1.D10, R4.Pin_0
  N2: Part1.D9, R5.Pin_0
  N3: Part1.D8, R6.Pin_0
  N4: Part1.D5, R2.Pin_0
  N5: Part1.D4, R3.Pin_0
  N6: Part1.D3, R1.Pin_0
  N7: Part1.GND, LED1.blue_cathode, LED2.blue_cathode
  N8: R1.Pin_1, LED1.green_cathode
  N9: R2.Pin_1, LED1.red_cathode
  N10: R3.Pin_1, LED1.common_anode
  N11: R4.Pin_1, LED2.red_cathode
  N12: R5.Pin_1, LED2.common_anode
  N13: R6.Pin_1, LED2.green_cathode

custom parts:
  Adafruit Metro M0 Express: Metro is our series of microcontroller boards for use with the Arduino IDE. This new Metro board looks a whole lot like our original Metro 328, but with a huge upgrade. Instead of the ATmega328, this Metro features a ATSAMD21G18 chip, an ARM Cortex M0+. It's our first Metro that is designed for use with CircuitPython! CircuitPython is our beginner-oriented flavor of MicroPython - and as the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
